// Logisim project project-miniCPU.circ as structural Verilog: 12 circuits, main circuit main
module main (
  output [2:0] Status
);

  wire ADD_or_SUB_out, ADD_q, and_1_out, and_3_out, and_4_out, and_5_out, and_6_out, and_7_out, and_8_out,
       and_9_out, and_10_out, and_11_out, and_13_out, and_14_out, and_15_out, and_16_out, and_17_out,
       and_18_out, and_19_out, and_20_out, and_21_out, and_22_out, and_23_out, and_24_out, and_25_out,
       and_26_out, and_27_out, bi1_change_out, bit0_change_out, bit2_change_out, bit3_change_out, clk,
       clock_1_out, controlled_buffer_1_out, controlled_buffer_9_out, controlled_buffer_17_out,
       controlled_buffer_25_out, controlled_buffer_33_out, controlled_buffer_35_out,
       controlled_buffer_37_out, controlled_buffer_39_out, d_ff_1_q, d_ff_2_q, d_ff_3_q, d_ff_4_q, d_ff_5_q,
       d_ff_6_q, d_ff_7_q, d_ff_8_q, d_ff_9_q, d_ff_10_q, d_ff_11_q, d_ff_12_q, d_ff_13_q, d_ff_14_q,
       d_ff_15_q, d_ff_16_q, d_ff_17_q, d_ff_18_q, d_ff_19_q, d_ff_20_q, d_ff_21_q, d_ff_22_q, d_ff_23_q,
       d_ff_24_q, d_ff_25_q, d_ff_26_q, d_ff_27_q, d_ff_28_q, d_ff_29_q, d_ff_30_q, d_ff_31_q, d_ff_32_q,
       d_ff_33_q, d_ff_34_q, d_ff_35_q, d_ff_36_q, d_ff_37_q, d_ff_38_q, d_ff_39_q, d_ff_40_q, d_ff_41_q,
       d_ff_42_q, d_ff_43_q, d_ff_44_q, d_ff_45_q, Data_in0_q, Data_in1_q, Data_in2_q, Data_in3_q,
       Data_input0_q, Data_input1_q, Data_input2_q, Data_input3_q, Data_RAM_Address_q, Data_RAM_Mode_q,
       decoder_1_out0, decoder_1_out1, decoder_1_out2, decoder_1_out3, decoder_1_out4, decoder_1_out5,
       decoder_1_out6, decoder_1_out7, decoder_2_out0, decoder_2_out1, decoder_2_out2, decoder_2_out3,
       decoder_3_out0, decoder_3_out1, fa_1_carryout, fa_2_carryout, halt, IR0_q, IR1_q, JumpEnable,
       LOAD_or_ADD_or_SUB_out, LOAD_q, LOAD_SAVE_Signal_out, Mode_q, not_1_out, not_2_out, not_3_out,
       not_4_out, not_5_out, not_6_out, not_7_out, or_1_out, or_2_out, or_3_out, or_4_out, R0_bit3_q,
       R1_bit0_q, R1_bit1_q, R1_bit2_q, R1_bit3_q, RAM_Address_Sel_or_Reg2_Sel_q, ready_q,
       Reg1_Sel_Delayed_q, Reg1_Sel_q, Reg2_Sel_Delayed_q, SAVE_q, SUB_q;
  wire [1:0] IR2_q;
  wire [2:0] Address_bit0_q, multiplexer_1_out, PC_Increment, PC_Out0_q, R0_bit0_q, R0_Output_Tunnel;
  wire [3:0] alu_a2_1_result, Data_out0_q, Data_output0_q, IR_q, multiplexer_2_out, multiplexer_6_out,
       multiplexer_10_out;

  not not_1 (not_1_out, halt);
  and and_1 (and_1_out, or_1_out, not_1_out, clk);
  D_Flip_Flop PC_Out0 (.D(multiplexer_1_out[0]), .clk(and_1_out), .Q(PC_Out0_q[0]));  // open: Qn, preset, reset
  D_Flip_Flop PC_Out1 (.D(multiplexer_1_out[1]), .clk(and_1_out), .Q(PC_Out0_q[1]));  // open: Qn, preset, reset
  D_Flip_Flop PC_Out2 (.D(multiplexer_1_out[2]), .clk(and_1_out), .Q(PC_Out0_q[2]));  // open: Qn, preset, reset
  Multiplexer #(.width(3)) multiplexer_1 (
    .in0(PC_Increment), .in1(R0_Output_Tunnel), .out(multiplexer_1_out), .sel(JumpEnable));
  FA fa_1 (.CarryIn(1'b0), .A(PC_Out0_q[0]), .B(1'b1), .Sum(PC_Increment[0]), .CarryOut(fa_1_carryout));
  FA fa_2 (.CarryIn(fa_1_carryout), .A(PC_Out0_q[1]), .B(1'b0), .Sum(PC_Increment[1]), .CarryOut(fa_2_carryout));
  FA fa_3 (.CarryIn(fa_2_carryout), .A(PC_Out0_q[2]), .B(1'b0), .Sum(PC_Increment[2]));  // open: CarryOut
  Clock clock_1 (.out(clock_1_out));
  and and_2 (clk, ~halt, clock_1_out);  // AND_Gate
  D_Flip_Flop Address_bit2 (.D(PC_Out0_q[2]), .clk(clk), .Q(Address_bit0_q[2]));  // open: Qn, preset, reset
  D_Flip_Flop Address_bit1 (.D(PC_Out0_q[1]), .clk(clk), .Q(Address_bit0_q[1]));  // open: Qn, preset, reset
  D_Flip_Flop Mode (.clk(clk), .Q(Mode_q));  // open: D, Qn, preset, reset
  D_Flip_Flop Address_bit0 (.D(PC_Out0_q[0]), .clk(clk), .Q(Address_bit0_q[0]));  // open: Qn, preset, reset
  Decoder #(.enable("false"), .select(3)) decoder_1 (
    .out0(decoder_1_out0), .out1(decoder_1_out1), .out2(decoder_1_out2), .out3(decoder_1_out3),
    .out4(decoder_1_out4), .out5(decoder_1_out5), .out6(decoder_1_out6), .out7(decoder_1_out7),
    .sel(Address_bit0_q));
  not not_2 (not_2_out, Mode_q);
  and and_3 (and_3_out, clk, Mode_q);
  and and_4 (and_4_out, not_2_out, clk, decoder_1_out0);
  and and_5 (and_5_out, decoder_1_out1, clk, not_2_out);
  and and_6 (and_6_out, not_2_out, clk, decoder_1_out2);
  and and_7 (and_7_out, not_2_out, clk, decoder_1_out3);
  and and_8 (and_8_out, not_2_out, clk, decoder_1_out4);
  and and_9 (and_9_out, decoder_1_out5, clk, not_2_out);
  and and_10 (and_10_out, not_2_out, clk, decoder_1_out6);
  and and_11 (and_11_out, not_2_out, clk, decoder_1_out7);
  D_Flip_Flop Data_input3 (.clk(clk), .Q(Data_input3_q));  // open: D, Qn, preset, reset
  D_Flip_Flop d_ff_1 (.D(Data_input3_q), .clk(and_4_out), .Q(d_ff_1_q));  // open: Qn, preset, reset
  D_Flip_Flop d_ff_2 (.D(Data_input3_q), .clk(and_5_out), .Q(d_ff_2_q));  // open: Qn, preset, reset
  D_Flip_Flop d_ff_3 (.D(Data_input3_q), .clk(and_6_out), .Q(d_ff_3_q));  // open: Qn, preset, reset
  D_Flip_Flop d_ff_4 (.D(Data_input3_q), .clk(and_7_out), .Q(d_ff_4_q));  // open: Qn, preset, reset
  D_Flip_Flop d_ff_5 (.D(Data_input3_q), .clk(and_8_out), .Q(d_ff_5_q));  // open: Qn, preset, reset
  D_Flip_Flop d_ff_6 (.D(Data_input3_q), .clk(and_9_out), .Q(d_ff_6_q));  // open: Qn, preset, reset
  D_Flip_Flop d_ff_7 (.D(Data_input3_q), .clk(and_10_out), .Q(d_ff_7_q));  // open: Qn, preset, reset
  D_Flip_Flop d_ff_8 (.D(Data_input3_q), .clk(and_11_out), .Q(d_ff_8_q));  // open: Qn, preset, reset
  assign controlled_buffer_1_out = decoder_1_out0 ? d_ff_1_q : 1'bz;  // Controlled_Buffer controlled_buffer_1
  assign controlled_buffer_1_out = decoder_1_out1 ? d_ff_2_q : 1'bz;  // Controlled_Buffer controlled_buffer_2
  assign controlled_buffer_1_out = decoder_1_out2 ? d_ff_3_q : 1'bz;  // Controlled_Buffer controlled_buffer_3
  assign controlled_buffer_1_out = decoder_1_out3 ? d_ff_4_q : 1'bz;  // Controlled_Buffer controlled_buffer_4
  assign controlled_buffer_1_out = decoder_1_out4 ? d_ff_5_q : 1'bz;  // Controlled_Buffer controlled_buffer_5
  assign controlled_buffer_1_out = decoder_1_out5 ? d_ff_6_q : 1'bz;  // Controlled_Buffer controlled_buffer_6
  assign controlled_buffer_1_out = decoder_1_out6 ? d_ff_7_q : 1'bz;  // Controlled_Buffer controlled_buffer_7
  assign controlled_buffer_1_out = decoder_1_out7 ? d_ff_8_q : 1'bz;  // Controlled_Buffer controlled_buffer_8
  D_Flip_Flop Data_input2 (.clk(clk), .Q(Data_input2_q));  // open: D, Qn, preset, reset
  D_Flip_Flop Data_output3 (
    .D(controlled_buffer_1_out), .clk(and_3_out), .Q(Data_output0_q[3]));  // open: Qn, preset, reset
  D_Flip_Flop d_ff_9 (.D(Data_input2_q), .clk(and_4_out), .Q(d_ff_9_q));  // open: Qn, preset, reset
  D_Flip_Flop d_ff_10 (.D(Data_input2_q), .clk(and_5_out), .Q(d_ff_10_q));  // open: Qn, preset, reset
  D_Flip_Flop d_ff_11 (.D(Data_input2_q), .clk(and_6_out), .Q(d_ff_11_q));  // open: Qn, preset, reset
  D_Flip_Flop d_ff_12 (.D(Data_input2_q), .clk(and_7_out), .Q(d_ff_12_q));  // open: Qn, preset, reset
  D_Flip_Flop d_ff_13 (.D(Data_input2_q), .clk(and_8_out), .Q(d_ff_13_q));  // open: Qn, preset, reset
  D_Flip_Flop d_ff_14 (.D(Data_input2_q), .clk(and_9_out), .Q(d_ff_14_q));  // open: Qn, preset, reset
  D_Flip_Flop d_ff_15 (.D(Data_input2_q), .clk(and_10_out), .Q(d_ff_15_q));  // open: Qn, preset, reset
  D_Flip_Flop d_ff_16 (.D(Data_input2_q), .clk(and_11_out), .Q(d_ff_16_q));  // open: Qn, preset, reset
  assign controlled_buffer_9_out = decoder_1_out0 ? d_ff_9_q : 1'bz;  // Controlled_Buffer controlled_buffer_9
  assign controlled_buffer_9_out = decoder_1_out1 ? d_ff_10_q : 1'bz;  // Controlled_Buffer controlled_buffer_10
  assign controlled_buffer_9_out = decoder_1_out2 ? d_ff_11_q : 1'bz;  // Controlled_Buffer controlled_buffer_11
  assign controlled_buffer_9_out = decoder_1_out3 ? d_ff_12_q : 1'bz;  // Controlled_Buffer controlled_buffer_12
  assign controlled_buffer_9_out = decoder_1_out4 ? d_ff_13_q : 1'bz;  // Controlled_Buffer controlled_buffer_13
  assign controlled_buffer_9_out = decoder_1_out5 ? d_ff_14_q : 1'bz;  // Controlled_Buffer controlled_buffer_14
  assign controlled_buffer_9_out = decoder_1_out6 ? d_ff_15_q : 1'bz;  // Controlled_Buffer controlled_buffer_15
  assign controlled_buffer_9_out = decoder_1_out7 ? d_ff_16_q : 1'bz;  // Controlled_Buffer controlled_buffer_16
  D_Flip_Flop Data_input1 (.clk(clk), .Q(Data_input1_q));  // open: D, Qn, preset, reset
  D_Flip_Flop Data_output2 (
    .D(controlled_buffer_9_out), .clk(and_3_out), .Q(Data_output0_q[2]));  // open: Qn, preset, reset
  D_Flip_Flop d_ff_17 (.D(Data_input1_q), .clk(and_4_out), .Q(d_ff_17_q));  // open: Qn, preset, reset
  D_Flip_Flop d_ff_18 (.D(Data_input1_q), .clk(and_5_out), .Q(d_ff_18_q));  // open: Qn, preset, reset
  D_Flip_Flop d_ff_19 (.D(Data_input1_q), .clk(and_6_out), .Q(d_ff_19_q));  // open: Qn, preset, reset
  D_Flip_Flop d_ff_20 (.D(Data_input1_q), .clk(and_7_out), .Q(d_ff_20_q));  // open: Qn, preset, reset
  D_Flip_Flop d_ff_21 (.D(Data_input1_q), .clk(and_8_out), .Q(d_ff_21_q));  // open: Qn, preset, reset
  D_Flip_Flop d_ff_22 (.D(Data_input1_q), .clk(and_9_out), .Q(d_ff_22_q));  // open: Qn, preset, reset
  D_Flip_Flop d_ff_23 (.D(Data_input1_q), .clk(and_10_out), .Q(d_ff_23_q));  // open: Qn, preset, reset
  D_Flip_Flop d_ff_24 (.D(Data_input1_q), .clk(and_11_out), .Q(d_ff_24_q));  // open: Qn, preset, reset
  assign controlled_buffer_17_out = decoder_1_out0 ? d_ff_17_q : 1'bz;  // Controlled_Buffer controlled_buffer_17
  assign controlled_buffer_17_out = decoder_1_out1 ? d_ff_18_q : 1'bz;  // Controlled_Buffer controlled_buffer_18
  assign controlled_buffer_17_out = decoder_1_out2 ? d_ff_19_q : 1'bz;  // Controlled_Buffer controlled_buffer_19
  assign controlled_buffer_17_out = decoder_1_out3 ? d_ff_20_q : 1'bz;  // Controlled_Buffer controlled_buffer_20
  assign controlled_buffer_17_out = decoder_1_out4 ? d_ff_21_q : 1'bz;  // Controlled_Buffer controlled_buffer_21
  assign controlled_buffer_17_out = decoder_1_out5 ? d_ff_22_q : 1'bz;  // Controlled_Buffer controlled_buffer_22
  assign controlled_buffer_17_out = decoder_1_out6 ? d_ff_23_q : 1'bz;  // Controlled_Buffer controlled_buffer_23
  assign controlled_buffer_17_out = decoder_1_out7 ? d_ff_24_q : 1'bz;  // Controlled_Buffer controlled_buffer_24
  D_Flip_Flop Data_input0 (.clk(clk), .Q(Data_input0_q));  // open: D, Qn, preset, reset
  D_Flip_Flop Data_output1 (
    .D(controlled_buffer_17_out), .clk(and_3_out), .Q(Data_output0_q[1]));  // open: Qn, preset, reset
  D_Flip_Flop d_ff_25 (.D(Data_input0_q), .clk(and_4_out), .Q(d_ff_25_q));  // open: Qn, preset, reset
  D_Flip_Flop d_ff_26 (.D(Data_input0_q), .clk(and_5_out), .Q(d_ff_26_q));  // open: Qn, preset, reset
  D_Flip_Flop d_ff_27 (.D(Data_input0_q), .clk(and_6_out), .Q(d_ff_27_q));  // open: Qn, preset, reset
  D_Flip_Flop d_ff_28 (.D(Data_input0_q), .clk(and_7_out), .Q(d_ff_28_q));  // open: Qn, preset, reset
  D_Flip_Flop d_ff_29 (.D(Data_input0_q), .clk(and_8_out), .Q(d_ff_29_q));  // open: Qn, preset, reset
  D_Flip_Flop d_ff_30 (.D(Data_input0_q), .clk(and_9_out), .Q(d_ff_30_q));  // open: Qn, preset, reset
  D_Flip_Flop d_ff_31 (.D(Data_input0_q), .clk(and_10_out), .Q(d_ff_31_q));  // open: Qn, preset, reset
  D_Flip_Flop d_ff_32 (.D(Data_input0_q), .clk(and_11_out), .Q(d_ff_32_q));  // open: Qn, preset, reset
  assign controlled_buffer_25_out = decoder_1_out0 ? d_ff_25_q : 1'bz;  // Controlled_Buffer controlled_buffer_25
  assign controlled_buffer_25_out = decoder_1_out1 ? d_ff_26_q : 1'bz;  // Controlled_Buffer controlled_buffer_26
  assign controlled_buffer_25_out = decoder_1_out2 ? d_ff_27_q : 1'bz;  // Controlled_Buffer controlled_buffer_27
  assign controlled_buffer_25_out = decoder_1_out3 ? d_ff_28_q : 1'bz;  // Controlled_Buffer controlled_buffer_28
  assign controlled_buffer_25_out = decoder_1_out4 ? d_ff_29_q : 1'bz;  // Controlled_Buffer controlled_buffer_29
  assign controlled_buffer_25_out = decoder_1_out5 ? d_ff_30_q : 1'bz;  // Controlled_Buffer controlled_buffer_30
  assign controlled_buffer_25_out = decoder_1_out6 ? d_ff_31_q : 1'bz;  // Controlled_Buffer controlled_buffer_31
  assign controlled_buffer_25_out = decoder_1_out7 ? d_ff_32_q : 1'bz;  // Controlled_Buffer controlled_buffer_32
  D_Flip_Flop Data_output0 (
    .D(controlled_buffer_25_out), .clk(and_3_out), .Q(Data_output0_q[0]));  // open: Qn, preset, reset
  not not_3 (not_3_out, Data_output0_q[3]);
  not not_4 (not_4_out, Data_output0_q[2]);
  not not_5 (not_5_out, Data_output0_q[1]);
  not not_6 (not_6_out, Data_output0_q[0]);
  and and_12 (JumpEnable, not_3_out, not_4_out, not_5_out, not_6_out);
  Register #(.width(4)) IR (.D(Data_output0_q), .clk(clk), .Q(IR_q));  // open: en, clr
  and u_HALT (halt, IR_q[0], IR_q[3]);
  xor bit0_change (bit0_change_out, Data_output0_q[0], IR_q[0]);
  xor bi1_change (bi1_change_out, Data_output0_q[1], IR_q[1]);
  xor bit2_change (bit2_change_out, Data_output0_q[2], IR_q[2]);
  xor bit3_change (bit3_change_out, Data_output0_q[3], IR_q[3]);
  or or_1 (or_1_out, bit0_change_out, bi1_change_out, bit2_change_out, bit3_change_out);
  D_Flip_Flop ready (.D(or_1_out), .clk(clk), .Q(ready_q));  // open: Qn, preset, reset
  D_Flip_Flop IR0 (.D(IR_q[0]), .clk(clk), .Q(IR0_q));  // open: Qn, preset, reset
  D_Flip_Flop IR1 (.D(IR_q[1]), .clk(clk), .Q(IR1_q));  // open: Qn, preset, reset
  D_Flip_Flop IR2 (.D(IR_q[2]), .clk(clk), .Q(IR2_q[0]));  // open: Qn, preset, reset
  D_Flip_Flop IR3 (.D(IR_q[3]), .clk(clk), .Q(IR2_q[1]));  // open: Qn, preset, reset
  D_Flip_Flop d_ff_33 (.D(ready_q), .clk(clk), .Q(d_ff_33_q));  // open: Qn, preset, reset
  Decoder #(.enable("false"), .select(2)) decoder_2 (
    .out0(decoder_2_out0), .out1(decoder_2_out1), .out2(decoder_2_out2), .out3(decoder_2_out3), .sel(IR2_q));
  and and_13 (and_13_out, IR0_q, IR1_q, IR2_q[0], IR2_q[1]);
  and and_14 (and_14_out, ~IR0_q, ~IR1_q, ~IR2_q[0], ~IR2_q[1]);  // AND_Gate
  or or_2 (or_2_out, and_21_out, and_22_out);
  and and_15 (and_15_out, or_2_out, and_17_out);
  and and_16 (and_16_out, or_2_out, and_18_out);
  and and_17 (and_17_out, d_ff_33_q, IR1_q);
  and and_18 (and_18_out, d_ff_33_q, IR0_q);
  and and_19 (and_19_out, d_ff_33_q, ~and_14_out, decoder_2_out0);  // AND_Gate
  and and_20 (and_20_out, d_ff_33_q, decoder_2_out1);
  and and_21 (and_21_out, d_ff_33_q, decoder_2_out2);
  and and_22 (and_22_out, d_ff_33_q, ~and_13_out, decoder_2_out3);  // AND_Gate
  D_Flip_Flop #(.trigger("falling")) Reg1_Sel_Delayed (
    .D(and_15_out), .clk(clk), .Q(Reg1_Sel_Delayed_q));  // open: Qn, preset, reset
  D_Flip_Flop #(.trigger("falling")) Reg2_Sel_Delayed (
    .D(and_16_out), .clk(clk), .Q(Reg2_Sel_Delayed_q));  // open: Qn, preset, reset
  D_Flip_Flop #(.trigger("falling")) Reg1_Sel (.D(and_17_out), .clk(clk), .Q(Reg1_Sel_q));  // open: Qn, preset, reset
  D_Flip_Flop #(.trigger("falling")) RAM_Address_Sel_or_Reg2_Sel (
    .D(and_18_out), .clk(clk), .Q(RAM_Address_Sel_or_Reg2_Sel_q));  // open: Qn, preset, reset
  D_Flip_Flop #(.trigger("falling")) LOAD (.D(and_19_out), .clk(clk), .Q(LOAD_q));  // open: Qn, preset, reset
  D_Flip_Flop #(.trigger("falling")) SAVE (.D(and_20_out), .clk(clk), .Q(SAVE_q));  // open: Qn, preset, reset
  D_Flip_Flop #(.trigger("falling")) ADD (.D(and_21_out), .clk(clk), .Q(ADD_q));  // open: Qn, preset, reset
  D_Flip_Flop #(.trigger("falling")) SUB (.D(and_22_out), .clk(clk), .Q(SUB_q));  // open: Qn, preset, reset
  or or_3 (or_3_out, d_ff_34_q, Reg1_Sel_q);
  D_Flip_Flop #(.trigger("falling")) d_ff_34 (
    .D(Reg1_Sel_Delayed_q), .clk(clk), .Q(d_ff_34_q));  // open: Qn, preset, reset
  D_Flip_Flop #(.trigger("falling")) d_ff_35 (
    .D(Reg2_Sel_Delayed_q), .clk(clk), .Q(d_ff_35_q));  // open: Qn, preset, reset
  D_Flip_Flop #(.trigger("falling")) d_ff_36 (.D(ADD_q), .clk(clk), .Q(d_ff_36_q));  // open: Qn, preset, reset
  D_Flip_Flop #(.trigger("falling")) d_ff_37 (.D(SUB_q), .clk(clk), .Q(d_ff_37_q));  // open: Qn, preset, reset
  or or_4 (or_4_out, d_ff_35_q, RAM_Address_Sel_or_Reg2_Sel_q);
  or ADD_or_SUB (ADD_or_SUB_out, d_ff_36_q, d_ff_37_q);
  or LOAD_or_ADD_or_SUB (LOAD_or_ADD_or_SUB_out, LOAD_q, d_ff_36_q, d_ff_37_q);
  and and_23 (and_23_out, ~or_3_out, clk, LOAD_or_ADD_or_SUB_out);  // AND_Gate
  and and_24 (and_24_out, or_3_out, clk, LOAD_or_ADD_or_SUB_out);
  D_Flip_Flop R0_bit3 (.D(multiplexer_2_out[3]), .clk(and_23_out), .Q(R0_bit3_q));  // open: Qn, preset, reset
  D_Flip_Flop R1_bit3 (.D(multiplexer_2_out[3]), .clk(and_24_out), .Q(R1_bit3_q));  // open: Qn, preset, reset
  D_Flip_Flop R0_bit2 (.D(multiplexer_2_out[2]), .clk(and_23_out), .Q(R0_bit0_q[2]));  // open: Qn, preset, reset
  D_Flip_Flop R1_bit2 (.D(multiplexer_2_out[2]), .clk(and_24_out), .Q(R1_bit2_q));  // open: Qn, preset, reset
  D_Flip_Flop R0_bit1 (.D(multiplexer_2_out[1]), .clk(and_23_out), .Q(R0_bit0_q[1]));  // open: Qn, preset, reset
  D_Flip_Flop R1_bit1 (.D(multiplexer_2_out[1]), .clk(and_24_out), .Q(R1_bit1_q));  // open: Qn, preset, reset
  Multiplexer multiplexer_2 (
    .in0(Data_out0_q[0]), .in1(alu_a2_1_result[0]), .out(multiplexer_2_out[0]), .sel(ADD_or_SUB_out));
  Multiplexer multiplexer_3 (
    .in0(Data_out0_q[1]), .in1(alu_a2_1_result[1]), .out(multiplexer_2_out[1]), .sel(ADD_or_SUB_out));
  Multiplexer multiplexer_4 (
    .in0(Data_out0_q[2]), .in1(alu_a2_1_result[2]), .out(multiplexer_2_out[2]), .sel(ADD_or_SUB_out));
  Multiplexer multiplexer_5 (
    .in0(Data_out0_q[3]), .in1(alu_a2_1_result[3]), .out(multiplexer_2_out[3]), .sel(ADD_or_SUB_out));
  D_Flip_Flop R0_bit0 (.D(multiplexer_2_out[0]), .clk(and_23_out), .Q(R0_bit0_q[0]));  // open: Qn, preset, reset
  D_Flip_Flop R1_bit0 (.D(multiplexer_2_out[0]), .clk(and_24_out), .Q(R1_bit0_q));  // open: Qn, preset, reset
  Multiplexer multiplexer_6 (.in0(R0_bit0_q[0]), .in1(R1_bit0_q), .out(multiplexer_6_out[0]), .sel(or_3_out));
  Multiplexer multiplexer_7 (.in0(R0_bit0_q[1]), .in1(R1_bit1_q), .out(multiplexer_6_out[1]), .sel(or_3_out));
  Multiplexer multiplexer_8 (.in0(R0_bit0_q[2]), .in1(R1_bit2_q), .out(multiplexer_6_out[2]), .sel(or_3_out));
  Multiplexer multiplexer_9 (.in0(R0_bit3_q), .in1(R1_bit3_q), .out(multiplexer_6_out[3]), .sel(or_3_out));
  Multiplexer multiplexer_10 (.in0(R0_bit0_q[0]), .in1(R1_bit0_q), .out(multiplexer_10_out[0]), .sel(or_4_out));
  Multiplexer multiplexer_11 (.in0(R0_bit0_q[1]), .in1(R1_bit1_q), .out(multiplexer_10_out[1]), .sel(or_4_out));
  Multiplexer multiplexer_12 (.in0(R0_bit0_q[2]), .in1(R1_bit2_q), .out(multiplexer_10_out[2]), .sel(or_4_out));
  Multiplexer multiplexer_13 (.in0(R0_bit3_q), .in1(R1_bit3_q), .out(multiplexer_10_out[3]), .sel(or_4_out));
  Register #(.width(3)) register_1 (.D(R0_bit0_q), .clk(clk), .Q(R0_Output_Tunnel));  // open: en, clr
  and LOAD_SAVE_Signal (LOAD_SAVE_Signal_out, LOAD_q, ~SAVE_q);  // AND_Gate
  ALU_A2 alu_a2_1 (
    .Binvert(SUB_q), .Ainvert(1'b0), .Operation(2'b10), .A(multiplexer_6_out), .Clk(clk),
    .B(multiplexer_10_out), .Result(alu_a2_1_result), .Status(Status));  // open: CarryOut
  D_Flip_Flop Data_RAM_Mode (.D(LOAD_SAVE_Signal_out), .clk(clk), .Q(Data_RAM_Mode_q));  // open: Qn, preset, reset
  Decoder #(.enable("false")) decoder_3 (.out0(decoder_3_out0), .out1(decoder_3_out1), .sel(Data_RAM_Address_q));
  not not_7 (not_7_out, Data_RAM_Mode_q);
  D_Flip_Flop Data_RAM_Address (.D(or_4_out), .clk(clk), .Q(Data_RAM_Address_q));  // open: Qn, preset, reset
  and and_25 (and_25_out, clk, Data_RAM_Mode_q);
  and and_26 (and_26_out, not_7_out, clk, decoder_3_out0);
  and and_27 (and_27_out, decoder_3_out1, clk, not_7_out);
  D_Flip_Flop Data_in3 (.D(multiplexer_6_out[3]), .clk(clk), .Q(Data_in3_q));  // open: Qn, preset, reset
  D_Flip_Flop d_ff_38 (.D(Data_in3_q), .clk(and_26_out), .Q(d_ff_38_q));  // open: Qn, preset, reset
  D_Flip_Flop d_ff_39 (.D(Data_in3_q), .clk(and_27_out), .Q(d_ff_39_q));  // open: Qn, preset, reset
  D_Flip_Flop Data_out3 (
    .D(controlled_buffer_33_out), .clk(and_25_out), .Q(Data_out0_q[3]));  // open: Qn, preset, reset
  assign controlled_buffer_33_out = decoder_3_out0 ? d_ff_38_q : 1'bz;  // Controlled_Buffer controlled_buffer_33
  assign controlled_buffer_33_out = decoder_3_out1 ? d_ff_39_q : 1'bz;  // Controlled_Buffer controlled_buffer_34
  D_Flip_Flop Data_in2 (.D(multiplexer_6_out[2]), .clk(clk), .Q(Data_in2_q));  // open: Qn, preset, reset
  D_Flip_Flop d_ff_40 (.D(Data_in2_q), .clk(and_26_out), .Q(d_ff_40_q));  // open: Qn, preset, reset
  D_Flip_Flop d_ff_41 (.D(Data_in2_q), .clk(and_27_out), .Q(d_ff_41_q));  // open: Qn, preset, reset
  D_Flip_Flop Data_out2 (
    .D(controlled_buffer_35_out), .clk(and_25_out), .Q(Data_out0_q[2]));  // open: Qn, preset, reset
  assign controlled_buffer_35_out = decoder_3_out0 ? d_ff_40_q : 1'bz;  // Controlled_Buffer controlled_buffer_35
  assign controlled_buffer_35_out = decoder_3_out1 ? d_ff_41_q : 1'bz;  // Controlled_Buffer controlled_buffer_36
  D_Flip_Flop Data_in1 (.D(multiplexer_6_out[1]), .clk(clk), .Q(Data_in1_q));  // open: Qn, preset, reset
  D_Flip_Flop d_ff_42 (.D(Data_in1_q), .clk(and_26_out), .Q(d_ff_42_q));  // open: Qn, preset, reset
  D_Flip_Flop d_ff_43 (.D(Data_in1_q), .clk(and_27_out), .Q(d_ff_43_q));  // open: Qn, preset, reset
  assign controlled_buffer_37_out = decoder_3_out0 ? d_ff_42_q : 1'bz;  // Controlled_Buffer controlled_buffer_37
  assign controlled_buffer_37_out = decoder_3_out1 ? d_ff_43_q : 1'bz;  // Controlled_Buffer controlled_buffer_38
  D_Flip_Flop Data_in0 (.D(multiplexer_6_out[0]), .clk(clk), .Q(Data_in0_q));  // open: Qn, preset, reset
  D_Flip_Flop Data_out1 (
    .D(controlled_buffer_37_out), .clk(and_25_out), .Q(Data_out0_q[1]));  // open: Qn, preset, reset
  D_Flip_Flop d_ff_44 (.D(Data_in0_q), .clk(and_26_out), .Q(d_ff_44_q));  // open: Qn, preset, reset
  D_Flip_Flop d_ff_45 (.D(Data_in0_q), .clk(and_27_out), .Q(d_ff_45_q));  // open: Qn, preset, reset
  D_Flip_Flop Data_out0 (
    .D(controlled_buffer_39_out), .clk(and_25_out), .Q(Data_out0_q[0]));  // open: Qn, preset, reset
  assign controlled_buffer_39_out = decoder_3_out0 ? d_ff_44_q : 1'bz;  // Controlled_Buffer controlled_buffer_39
  assign controlled_buffer_39_out = decoder_3_out1 ? d_ff_45_q : 1'bz;  // Controlled_Buffer controlled_buffer_40

  // Notes on the sheet:
  //   Colette Li  261098318
  //   Ece Goksu  261138642
  //   PC
  //   Instruction RAM (A2)
  //   please input instruction by directly toggling output d flip flops
  //   IR
  //   CU
  //   Opcode
  //   Register R0
  //   Register R1
  //   Register File
  //   Reg1_Select
  //   Reg2_Select
  //   ALU (A2)
  //   Data RAM (A2)
  //   please input data by directly toggling output d flip flops
endmodule

module PC (
  input  WE,
  input  Clk,
  output [2:0] PC_Out
);

  wire fa_1_carryout, fa_2_carryout;
  wire [2:0] fa_1_sum;

  Register #(.width(3)) register_1 (.D(fa_1_sum), .en(WE), .clk(Clk), .Q(PC_Out));  // open: clr
  FA fa_1 (.CarryIn(1'b0), .A(PC_Out[0]), .B(1'b1), .Sum(fa_1_sum[0]), .CarryOut(fa_1_carryout));
  FA fa_2 (.CarryIn(fa_1_carryout), .A(PC_Out[1]), .B(1'b0), .Sum(fa_1_sum[1]), .CarryOut(fa_2_carryout));
  FA fa_3 (.CarryIn(fa_2_carryout), .A(PC_Out[2]), .B(1'b0), .Sum(fa_1_sum[2]));  // open: CarryOut
endmodule

module Instruction_RAM_A2 (
  input  Clk,
  input  Mode,
  input  [2:0] Address,
  input  [3:0] Data_input,
  output [3:0] Data_output
);

  wire and_1_out, and_2_out, and_3_out, and_4_out, and_5_out, and_6_out, and_7_out, and_8_out, and_9_out,
       controlled_buffer_1_out, controlled_buffer_9_out, controlled_buffer_17_out, controlled_buffer_25_out,
       d_ff_3_q, d_ff_5_q, d_ff_6_q, d_ff_7_q, d_ff_8_q, d_ff_9_q, d_ff_10_q, d_ff_11_q, d_ff_12_q,
       d_ff_13_q, d_ff_15_q, d_ff_16_q, d_ff_17_q, d_ff_18_q, d_ff_19_q, d_ff_20_q, d_ff_21_q, d_ff_22_q,
       d_ff_23_q, d_ff_24_q, d_ff_26_q, d_ff_27_q, d_ff_28_q, d_ff_29_q, d_ff_30_q, d_ff_31_q, d_ff_32_q,
       d_ff_33_q, d_ff_34_q, d_ff_36_q, d_ff_37_q, d_ff_38_q, d_ff_39_q, d_ff_40_q, d_ff_41_q, d_ff_42_q,
       d_ff_43_q, decoder_1_out0, decoder_1_out1, decoder_1_out2, decoder_1_out3, decoder_1_out4,
       decoder_1_out5, decoder_1_out6, decoder_1_out7, not_1_out;
  wire [2:0] d_ff_4_q;

  D_Flip_Flop d_ff_1 (.D(Address[2]), .clk(Clk), .Q(d_ff_4_q[2]));  // open: Qn, preset, reset
  D_Flip_Flop d_ff_2 (.D(Address[1]), .clk(Clk), .Q(d_ff_4_q[1]));  // open: Qn, preset, reset
  D_Flip_Flop d_ff_3 (.D(Mode), .clk(Clk), .Q(d_ff_3_q));  // open: Qn, preset, reset
  D_Flip_Flop d_ff_4 (.D(Address[0]), .clk(Clk), .Q(d_ff_4_q[0]));  // open: Qn, preset, reset
  Decoder #(.enable("false"), .select(3)) decoder_1 (
    .out0(decoder_1_out0), .out1(decoder_1_out1), .out2(decoder_1_out2), .out3(decoder_1_out3),
    .out4(decoder_1_out4), .out5(decoder_1_out5), .out6(decoder_1_out6), .out7(decoder_1_out7), .sel(d_ff_4_q));
  not not_1 (not_1_out, d_ff_3_q);
  and and_1 (and_1_out, not_1_out, Clk, decoder_1_out0);
  and and_2 (and_2_out, decoder_1_out1, Clk, not_1_out);
  and and_3 (and_3_out, not_1_out, Clk, decoder_1_out2);
  and and_4 (and_4_out, not_1_out, Clk, decoder_1_out3);
  and and_5 (and_5_out, not_1_out, Clk, decoder_1_out4);
  and and_6 (and_6_out, decoder_1_out5, Clk, not_1_out);
  and and_7 (and_7_out, not_1_out, Clk, decoder_1_out6);
  and and_8 (and_8_out, not_1_out, Clk, decoder_1_out7);
  and and_9 (and_9_out, Clk, d_ff_3_q);
  D_Flip_Flop d_ff_5 (.D(Data_input[3]), .clk(Clk), .Q(d_ff_5_q));  // open: Qn, preset, reset
  D_Flip_Flop d_ff_6 (.D(d_ff_5_q), .clk(and_1_out), .Q(d_ff_6_q));  // open: Qn, preset, reset
  D_Flip_Flop d_ff_7 (.D(d_ff_5_q), .clk(and_2_out), .Q(d_ff_7_q));  // open: Qn, preset, reset
  D_Flip_Flop d_ff_8 (.D(d_ff_5_q), .clk(and_3_out), .Q(d_ff_8_q));  // open: Qn, preset, reset
  D_Flip_Flop d_ff_9 (.D(d_ff_5_q), .clk(and_4_out), .Q(d_ff_9_q));  // open: Qn, preset, reset
  D_Flip_Flop d_ff_10 (.D(d_ff_5_q), .clk(and_5_out), .Q(d_ff_10_q));  // open: Qn, preset, reset
  D_Flip_Flop d_ff_11 (.D(d_ff_5_q), .clk(and_6_out), .Q(d_ff_11_q));  // open: Qn, preset, reset
  D_Flip_Flop d_ff_12 (.D(d_ff_5_q), .clk(and_7_out), .Q(d_ff_12_q));  // open: Qn, preset, reset
  D_Flip_Flop d_ff_13 (.D(d_ff_5_q), .clk(and_8_out), .Q(d_ff_13_q));  // open: Qn, preset, reset
  D_Flip_Flop d_ff_14 (.D(controlled_buffer_1_out), .clk(and_9_out), .Q(Data_output[3]));  // open: Qn, preset, reset
  assign controlled_buffer_1_out = decoder_1_out0 ? d_ff_6_q : 1'bz;  // Controlled_Buffer controlled_buffer_1
  assign controlled_buffer_1_out = decoder_1_out1 ? d_ff_7_q : 1'bz;  // Controlled_Buffer controlled_buffer_2
  assign controlled_buffer_1_out = decoder_1_out2 ? d_ff_8_q : 1'bz;  // Controlled_Buffer controlled_buffer_3
  assign controlled_buffer_1_out = decoder_1_out3 ? d_ff_9_q : 1'bz;  // Controlled_Buffer controlled_buffer_4
  assign controlled_buffer_1_out = decoder_1_out4 ? d_ff_10_q : 1'bz;  // Controlled_Buffer controlled_buffer_5
  assign controlled_buffer_1_out = decoder_1_out5 ? d_ff_11_q : 1'bz;  // Controlled_Buffer controlled_buffer_6
  assign controlled_buffer_1_out = decoder_1_out6 ? d_ff_12_q : 1'bz;  // Controlled_Buffer controlled_buffer_7
  assign controlled_buffer_1_out = decoder_1_out7 ? d_ff_13_q : 1'bz;  // Controlled_Buffer controlled_buffer_8
  D_Flip_Flop d_ff_15 (.D(Data_input[2]), .clk(Clk), .Q(d_ff_15_q));  // open: Qn, preset, reset
  D_Flip_Flop d_ff_16 (.D(d_ff_15_q), .clk(and_1_out), .Q(d_ff_16_q));  // open: Qn, preset, reset
  D_Flip_Flop d_ff_17 (.D(d_ff_15_q), .clk(and_2_out), .Q(d_ff_17_q));  // open: Qn, preset, reset
  D_Flip_Flop d_ff_18 (.D(d_ff_15_q), .clk(and_3_out), .Q(d_ff_18_q));  // open: Qn, preset, reset
  D_Flip_Flop d_ff_19 (.D(d_ff_15_q), .clk(and_4_out), .Q(d_ff_19_q));  // open: Qn, preset, reset
  D_Flip_Flop d_ff_20 (.D(d_ff_15_q), .clk(and_5_out), .Q(d_ff_20_q));  // open: Qn, preset, reset
  D_Flip_Flop d_ff_21 (.D(d_ff_15_q), .clk(and_6_out), .Q(d_ff_21_q));  // open: Qn, preset, reset
  D_Flip_Flop d_ff_22 (.D(d_ff_15_q), .clk(and_7_out), .Q(d_ff_22_q));  // open: Qn, preset, reset
  D_Flip_Flop d_ff_23 (.D(d_ff_15_q), .clk(and_8_out), .Q(d_ff_23_q));  // open: Qn, preset, reset
  assign controlled_buffer_9_out = decoder_1_out0 ? d_ff_16_q : 1'bz;  // Controlled_Buffer controlled_buffer_9
  assign controlled_buffer_9_out = decoder_1_out1 ? d_ff_17_q : 1'bz;  // Controlled_Buffer controlled_buffer_10
  assign controlled_buffer_9_out = decoder_1_out2 ? d_ff_18_q : 1'bz;  // Controlled_Buffer controlled_buffer_11
  assign controlled_buffer_9_out = decoder_1_out3 ? d_ff_19_q : 1'bz;  // Controlled_Buffer controlled_buffer_12
  assign controlled_buffer_9_out = decoder_1_out4 ? d_ff_20_q : 1'bz;  // Controlled_Buffer controlled_buffer_13
  assign controlled_buffer_9_out = decoder_1_out5 ? d_ff_21_q : 1'bz;  // Controlled_Buffer controlled_buffer_14
  assign controlled_buffer_9_out = decoder_1_out6 ? d_ff_22_q : 1'bz;  // Controlled_Buffer controlled_buffer_15
  assign controlled_buffer_9_out = decoder_1_out7 ? d_ff_23_q : 1'bz;  // Controlled_Buffer controlled_buffer_16
  D_Flip_Flop d_ff_24 (.D(Data_input[1]), .clk(Clk), .Q(d_ff_24_q));  // open: Qn, preset, reset
  D_Flip_Flop d_ff_25 (.D(controlled_buffer_9_out), .clk(and_9_out), .Q(Data_output[2]));  // open: Qn, preset, reset
  D_Flip_Flop d_ff_26 (.D(d_ff_24_q), .clk(and_1_out), .Q(d_ff_26_q));  // open: Qn, preset, reset
  D_Flip_Flop d_ff_27 (.D(d_ff_24_q), .clk(and_2_out), .Q(d_ff_27_q));  // open: Qn, preset, reset
  D_Flip_Flop d_ff_28 (.D(d_ff_24_q), .clk(and_3_out), .Q(d_ff_28_q));  // open: Qn, preset, reset
  D_Flip_Flop d_ff_29 (.D(d_ff_24_q), .clk(and_4_out), .Q(d_ff_29_q));  // open: Qn, preset, reset
  D_Flip_Flop d_ff_30 (.D(d_ff_24_q), .clk(and_5_out), .Q(d_ff_30_q));  // open: Qn, preset, reset
  D_Flip_Flop d_ff_31 (.D(d_ff_24_q), .clk(and_6_out), .Q(d_ff_31_q));  // open: Qn, preset, reset
  D_Flip_Flop d_ff_32 (.D(d_ff_24_q), .clk(and_7_out), .Q(d_ff_32_q));  // open: Qn, preset, reset
  D_Flip_Flop d_ff_33 (.D(d_ff_24_q), .clk(and_8_out), .Q(d_ff_33_q));  // open: Qn, preset, reset
  assign controlled_buffer_17_out = decoder_1_out0 ? d_ff_26_q : 1'bz;  // Controlled_Buffer controlled_buffer_17
  assign controlled_buffer_17_out = decoder_1_out1 ? d_ff_27_q : 1'bz;  // Controlled_Buffer controlled_buffer_18
  assign controlled_buffer_17_out = decoder_1_out2 ? d_ff_28_q : 1'bz;  // Controlled_Buffer controlled_buffer_19
  assign controlled_buffer_17_out = decoder_1_out3 ? d_ff_29_q : 1'bz;  // Controlled_Buffer controlled_buffer_20
  assign controlled_buffer_17_out = decoder_1_out4 ? d_ff_30_q : 1'bz;  // Controlled_Buffer controlled_buffer_21
  assign controlled_buffer_17_out = decoder_1_out5 ? d_ff_31_q : 1'bz;  // Controlled_Buffer controlled_buffer_22
  assign controlled_buffer_17_out = decoder_1_out6 ? d_ff_32_q : 1'bz;  // Controlled_Buffer controlled_buffer_23
  assign controlled_buffer_17_out = decoder_1_out7 ? d_ff_33_q : 1'bz;  // Controlled_Buffer controlled_buffer_24
  D_Flip_Flop d_ff_34 (.D(Data_input[0]), .clk(Clk), .Q(d_ff_34_q));  // open: Qn, preset, reset
  D_Flip_Flop d_ff_35 (.D(controlled_buffer_17_out), .clk(and_9_out), .Q(Data_output[1]));  // open: Qn, preset, reset
  D_Flip_Flop d_ff_36 (.D(d_ff_34_q), .clk(and_1_out), .Q(d_ff_36_q));  // open: Qn, preset, reset
  D_Flip_Flop d_ff_37 (.D(d_ff_34_q), .clk(and_2_out), .Q(d_ff_37_q));  // open: Qn, preset, reset
  D_Flip_Flop d_ff_38 (.D(d_ff_34_q), .clk(and_3_out), .Q(d_ff_38_q));  // open: Qn, preset, reset
  D_Flip_Flop d_ff_39 (.D(d_ff_34_q), .clk(and_4_out), .Q(d_ff_39_q));  // open: Qn, preset, reset
  D_Flip_Flop d_ff_40 (.D(d_ff_34_q), .clk(and_5_out), .Q(d_ff_40_q));  // open: Qn, preset, reset
  D_Flip_Flop d_ff_41 (.D(d_ff_34_q), .clk(and_6_out), .Q(d_ff_41_q));  // open: Qn, preset, reset
  D_Flip_Flop d_ff_42 (.D(d_ff_34_q), .clk(and_7_out), .Q(d_ff_42_q));  // open: Qn, preset, reset
  D_Flip_Flop d_ff_43 (.D(d_ff_34_q), .clk(and_8_out), .Q(d_ff_43_q));  // open: Qn, preset, reset
  assign controlled_buffer_25_out = decoder_1_out0 ? d_ff_36_q : 1'bz;  // Controlled_Buffer controlled_buffer_25
  assign controlled_buffer_25_out = decoder_1_out1 ? d_ff_37_q : 1'bz;  // Controlled_Buffer controlled_buffer_26
  assign controlled_buffer_25_out = decoder_1_out2 ? d_ff_38_q : 1'bz;  // Controlled_Buffer controlled_buffer_27
  assign controlled_buffer_25_out = decoder_1_out3 ? d_ff_39_q : 1'bz;  // Controlled_Buffer controlled_buffer_28
  assign controlled_buffer_25_out = decoder_1_out4 ? d_ff_40_q : 1'bz;  // Controlled_Buffer controlled_buffer_29
  assign controlled_buffer_25_out = decoder_1_out5 ? d_ff_41_q : 1'bz;  // Controlled_Buffer controlled_buffer_30
  assign controlled_buffer_25_out = decoder_1_out6 ? d_ff_42_q : 1'bz;  // Controlled_Buffer controlled_buffer_31
  assign controlled_buffer_25_out = decoder_1_out7 ? d_ff_43_q : 1'bz;  // Controlled_Buffer controlled_buffer_32
  D_Flip_Flop d_ff_44 (.D(controlled_buffer_25_out), .clk(and_9_out), .Q(Data_output[0]));  // open: Qn, preset, reset

  // Notes on the sheet:
  //   Colette Li 261098318
endmodule

module IR (
  input  Clk,
  input  In0,
  input  In1,
  input  In2,
  input  In3,
  output Out0,
  output Out1,
  output Out2,
  output Out3
);

  Register #(.width(4)) register_1 (
    .D({In3, In2, In1, In0}), .clk(Clk), .Q({Out3, Out2, Out1, Out0}));  // open: en, clr
endmodule

module Register_File (
  input  Clk,
  input  [3:0] R0_inputs,
  input  R0_WE,
  input  [3:0] R1_inputs,
  input  R1_WE,
  output [3:0] R0_outputs,
  output [3:0] R1_outputs
);

  Register #(.width(4)) R0 (.D(R0_inputs), .en(R0_WE), .clk(Clk), .Q(R0_outputs));  // open: clr
  Register #(.width(4)) R1 (.D(R1_inputs), .en(R1_WE), .clk(Clk), .Q(R1_outputs));  // open: clr
endmodule

module Data_RAM_A2 (
  input  Clk,
  input  Mode,
  input  Address,
  input  [3:0] Data_input,
  output [3:0] Data_output
);

  wire and_1_out, and_2_out, and_3_out, controlled_buffer_1_out, controlled_buffer_3_out,
       controlled_buffer_5_out, controlled_buffer_7_out, d_ff_1_q, d_ff_2_q, d_ff_3_q, d_ff_4_q, d_ff_5_q,
       d_ff_7_q, d_ff_8_q, d_ff_9_q, d_ff_11_q, d_ff_12_q, d_ff_13_q, d_ff_14_q, d_ff_16_q, d_ff_17_q,
       decoder_1_out0, decoder_1_out1, not_1_out;

  D_Flip_Flop d_ff_1 (.D(Mode), .clk(Clk), .Q(d_ff_1_q));  // open: Qn, preset, reset
  Decoder #(.enable("false")) decoder_1 (.out0(decoder_1_out0), .out1(decoder_1_out1), .sel(d_ff_2_q));
  D_Flip_Flop d_ff_2 (.D(Address), .clk(Clk), .Q(d_ff_2_q));  // open: Qn, preset, reset
  not not_1 (not_1_out, d_ff_1_q);
  and and_1 (and_1_out, not_1_out, Clk, decoder_1_out0);
  and and_2 (and_2_out, decoder_1_out1, Clk, not_1_out);
  and and_3 (and_3_out, Clk, d_ff_1_q);
  D_Flip_Flop d_ff_3 (.D(Data_input[3]), .clk(Clk), .Q(d_ff_3_q));  // open: Qn, preset, reset
  D_Flip_Flop d_ff_4 (.D(d_ff_3_q), .clk(and_1_out), .Q(d_ff_4_q));  // open: Qn, preset, reset
  D_Flip_Flop d_ff_5 (.D(d_ff_3_q), .clk(and_2_out), .Q(d_ff_5_q));  // open: Qn, preset, reset
  D_Flip_Flop d_ff_6 (.D(controlled_buffer_1_out), .clk(and_3_out), .Q(Data_output[3]));  // open: Qn, preset, reset
  assign controlled_buffer_1_out = decoder_1_out0 ? d_ff_4_q : 1'bz;  // Controlled_Buffer controlled_buffer_1
  assign controlled_buffer_1_out = decoder_1_out1 ? d_ff_5_q : 1'bz;  // Controlled_Buffer controlled_buffer_2
  D_Flip_Flop d_ff_7 (.D(Data_input[2]), .clk(Clk), .Q(d_ff_7_q));  // open: Qn, preset, reset
  D_Flip_Flop d_ff_8 (.D(d_ff_7_q), .clk(and_1_out), .Q(d_ff_8_q));  // open: Qn, preset, reset
  D_Flip_Flop d_ff_9 (.D(d_ff_7_q), .clk(and_2_out), .Q(d_ff_9_q));  // open: Qn, preset, reset
  D_Flip_Flop d_ff_10 (.D(controlled_buffer_3_out), .clk(and_3_out), .Q(Data_output[2]));  // open: Qn, preset, reset
  assign controlled_buffer_3_out = decoder_1_out0 ? d_ff_8_q : 1'bz;  // Controlled_Buffer controlled_buffer_3
  assign controlled_buffer_3_out = decoder_1_out1 ? d_ff_9_q : 1'bz;  // Controlled_Buffer controlled_buffer_4
  D_Flip_Flop d_ff_11 (.D(Data_input[1]), .clk(Clk), .Q(d_ff_11_q));  // open: Qn, preset, reset
  D_Flip_Flop d_ff_12 (.D(d_ff_11_q), .clk(and_1_out), .Q(d_ff_12_q));  // open: Qn, preset, reset
  D_Flip_Flop d_ff_13 (.D(d_ff_11_q), .clk(and_2_out), .Q(d_ff_13_q));  // open: Qn, preset, reset
  assign controlled_buffer_5_out = decoder_1_out0 ? d_ff_12_q : 1'bz;  // Controlled_Buffer controlled_buffer_5
  assign controlled_buffer_5_out = decoder_1_out1 ? d_ff_13_q : 1'bz;  // Controlled_Buffer controlled_buffer_6
  D_Flip_Flop d_ff_14 (.D(Data_input[0]), .clk(Clk), .Q(d_ff_14_q));  // open: Qn, preset, reset
  D_Flip_Flop d_ff_15 (.D(controlled_buffer_5_out), .clk(and_3_out), .Q(Data_output[1]));  // open: Qn, preset, reset
  D_Flip_Flop d_ff_16 (.D(d_ff_14_q), .clk(and_1_out), .Q(d_ff_16_q));  // open: Qn, preset, reset
  D_Flip_Flop d_ff_17 (.D(d_ff_14_q), .clk(and_2_out), .Q(d_ff_17_q));  // open: Qn, preset, reset
  assign controlled_buffer_7_out = decoder_1_out0 ? d_ff_16_q : 1'bz;  // Controlled_Buffer controlled_buffer_7
  assign controlled_buffer_7_out = decoder_1_out1 ? d_ff_17_q : 1'bz;  // Controlled_Buffer controlled_buffer_8
  D_Flip_Flop d_ff_18 (.D(controlled_buffer_7_out), .clk(and_3_out), .Q(Data_output[0]));  // open: Qn, preset, reset

  // Notes on the sheet:
  //   Colette Li 261098318
endmodule

module CU (
  input  ready,
  input  clk,
  input  IR0,
  input  IR1,
  input  IR2,
  input  IR3,
  output Reg1_Select,
  output RAM_Address_Select_or_Reg2_Select,
  output HALT,
  output JUMP,
  output LOAD,
  output SAVE,
  output ADD,
  output SUB
);

  wire and_1_out, and_2_out, and_3_out, and_4_out, and_5_out, and_6_out, and_7_out, and_8_out, and_9_out,
       and_10_out, d_ff_1_q, d_ff_2_q, d_ff_3_q, decoder_1_out0, decoder_1_out1, decoder_1_out2,
       decoder_1_out3;
  wire [1:0] d_ff_4_q;

  D_Flip_Flop d_ff_1 (.D(ready), .clk(clk), .Q(d_ff_1_q));  // open: Qn, preset, reset
  D_Flip_Flop d_ff_2 (.D(IR0), .clk(clk), .Q(d_ff_2_q));  // open: Qn, preset, reset
  D_Flip_Flop d_ff_3 (.D(IR1), .clk(clk), .Q(d_ff_3_q));  // open: Qn, preset, reset
  D_Flip_Flop d_ff_4 (.D(IR2), .clk(clk), .Q(d_ff_4_q[0]));  // open: Qn, preset, reset
  D_Flip_Flop d_ff_5 (.D(IR3), .clk(clk), .Q(d_ff_4_q[1]));  // open: Qn, preset, reset
  Decoder #(.enable("false"), .select(2)) decoder_1 (
    .out0(decoder_1_out0), .out1(decoder_1_out1), .out2(decoder_1_out2), .out3(decoder_1_out3), .sel(d_ff_4_q));
  and and_1 (and_1_out, d_ff_2_q, d_ff_3_q, d_ff_4_q[0], d_ff_4_q[1]);
  and and_2 (and_2_out, ~d_ff_2_q, ~d_ff_3_q, ~d_ff_4_q[0], ~d_ff_4_q[1]);  // AND_Gate
  and and_3 (and_3_out, d_ff_1_q, d_ff_3_q);
  and and_4 (and_4_out, d_ff_1_q, d_ff_2_q);
  and and_5 (and_5_out, d_ff_1_q, and_1_out);
  and and_6 (and_6_out, d_ff_1_q, and_2_out);
  and and_7 (and_7_out, d_ff_1_q, ~and_2_out, decoder_1_out0);  // AND_Gate
  and and_8 (and_8_out, d_ff_1_q, decoder_1_out1);
  and and_9 (and_9_out, d_ff_1_q, decoder_1_out2);
  and and_10 (and_10_out, d_ff_1_q, ~and_1_out, decoder_1_out3);  // AND_Gate
  D_Flip_Flop d_ff_6 (.D(and_3_out), .clk(clk), .Q(Reg1_Select));  // open: Qn, preset, reset
  D_Flip_Flop d_ff_7 (.D(and_4_out), .clk(clk), .Q(RAM_Address_Select_or_Reg2_Select));  // open: Qn, preset, reset
  D_Flip_Flop d_ff_8 (.D(and_5_out), .clk(clk), .Q(HALT));  // open: Qn, preset, reset
  D_Flip_Flop d_ff_9 (.D(and_6_out), .clk(clk), .Q(JUMP));  // open: Qn, preset, reset
  D_Flip_Flop d_ff_10 (.D(and_7_out), .clk(clk), .Q(LOAD));  // open: Qn, preset, reset
  D_Flip_Flop d_ff_11 (.D(and_8_out), .clk(clk), .Q(SAVE));  // open: Qn, preset, reset
  D_Flip_Flop d_ff_12 (.D(and_9_out), .clk(clk), .Q(ADD));  // open: Qn, preset, reset
  D_Flip_Flop d_ff_13 (.D(and_10_out), .clk(clk), .Q(SUB));  // open: Qn, preset, reset

  // Notes on the sheet:
  //   Opcode
endmodule

module ALU_A2 (
  input  Binvert,
  input  Ainvert,
  input  [1:0] Operation,
  input  [3:0] A,
  input  Clk,
  input  [3:0] B,
  output [3:0] Result,
  output [2:0] Status,
  output CarryOut
);

  wire and_1_out, and_2_out, and_3_out, and_4_out, and_5_out, and_6_out, and_7_out, and_8_out, and_9_out,
       and_10_out, and_11_out, and_13_out, and_14_out, and_15_out, and_16_out, fa_1_carryout, fa_1_sum,
       fa_2_carryout, fa_2_sum, fa_3_carryout, fa_3_sum, fa_4_sum, mux_2to1_1_o, mux_2to1_2_o, mux_2to1_3_o,
       mux_2to1_4_o, mux_2to1_5_o, mux_2to1_6_o, mux_2to1_7_o, mux_2to1_8_o, not_1_out, not_2_out, not_3_out,
       not_4_out, not_5_out, not_6_out, not_7_out, not_8_out, or_1_out, or_2_out, or_3_out, or_4_out,
       register_3_q, register_4_q, xor_1_out;
  wire [1:0] register_5_q;
  wire [2:0] and_17_out;
  wire [3:0] mux_3to1_1_o, register_1_q, register_2_q;

  Register #(.width(4)) register_1 (.D(A), .clk(Clk), .Q(register_1_q));  // open: en, clr
  Register #(.width(4)) register_2 (.D(B), .clk(Clk), .Q(register_2_q));  // open: en, clr
  Register #(.width(1)) register_3 (.D(Binvert), .clk(Clk), .Q(register_3_q));  // open: en, clr
  Register #(.width(1)) register_4 (.D(Ainvert), .clk(Clk), .Q(register_4_q));  // open: en, clr
  not not_1 (not_1_out, register_1_q[0]);
  not not_2 (not_2_out, register_1_q[1]);
  not not_3 (not_3_out, register_1_q[2]);
  not not_4 (not_4_out, register_1_q[3]);
  not not_5 (not_5_out, register_2_q[0]);
  not not_6 (not_6_out, register_2_q[1]);
  not not_7 (not_7_out, register_2_q[2]);
  not not_8 (not_8_out, register_2_q[3]);
  Mux_2to1 mux_2to1_1 (.S(register_4_q), .A(register_1_q[0]), .B(not_1_out), .O(mux_2to1_1_o));
  Mux_2to1 mux_2to1_2 (.S(register_4_q), .A(register_1_q[1]), .B(not_2_out), .O(mux_2to1_2_o));
  Mux_2to1 mux_2to1_3 (.S(register_4_q), .A(register_1_q[2]), .B(not_3_out), .O(mux_2to1_3_o));
  Mux_2to1 mux_2to1_4 (.S(register_4_q), .A(register_1_q[3]), .B(not_4_out), .O(mux_2to1_4_o));
  Mux_2to1 mux_2to1_5 (.S(register_3_q), .A(register_2_q[0]), .B(not_5_out), .O(mux_2to1_5_o));
  Mux_2to1 mux_2to1_6 (.S(register_3_q), .A(register_2_q[1]), .B(not_6_out), .O(mux_2to1_6_o));
  Mux_2to1 mux_2to1_7 (.S(register_3_q), .A(register_2_q[2]), .B(not_7_out), .O(mux_2to1_7_o));
  Mux_2to1 mux_2to1_8 (.S(register_3_q), .A(register_2_q[3]), .B(not_8_out), .O(mux_2to1_8_o));
  and and_1 (and_1_out, mux_2to1_1_o, mux_2to1_5_o);
  or or_1 (or_1_out, mux_2to1_1_o, mux_2to1_5_o);
  and and_2 (and_2_out, ~register_4_q, register_3_q, register_5_q[1], ~register_5_q[0]);  // AND_Gate
  and and_3 (and_3_out, mux_2to1_2_o, mux_2to1_6_o);
  or or_2 (or_2_out, mux_2to1_2_o, mux_2to1_6_o);
  and and_4 (and_4_out, mux_2to1_3_o, mux_2to1_7_o);
  or or_3 (or_3_out, mux_2to1_3_o, mux_2to1_7_o);
  and and_5 (and_5_out, mux_2to1_4_o, mux_2to1_8_o);
  or or_4 (or_4_out, mux_2to1_4_o, mux_2to1_8_o);
  Register #(.width(2)) register_5 (.D(Operation), .clk(Clk), .Q(register_5_q));  // open: en, clr
  FA fa_1 (.CarryIn(and_2_out), .A(mux_2to1_1_o), .B(mux_2to1_5_o), .Sum(fa_1_sum), .CarryOut(fa_1_carryout));
  FA fa_2 (.CarryIn(fa_1_carryout), .A(mux_2to1_2_o), .B(mux_2to1_6_o), .Sum(fa_2_sum), .CarryOut(fa_2_carryout));
  FA fa_3 (.CarryIn(fa_2_carryout), .A(mux_2to1_3_o), .B(mux_2to1_7_o), .Sum(fa_3_sum), .CarryOut(fa_3_carryout));
  FA fa_4 (.CarryIn(fa_3_carryout), .A(mux_2to1_4_o), .B(mux_2to1_8_o), .Sum(fa_4_sum), .CarryOut(CarryOut));
  Mux_3to1 mux_3to1_1 (
    .S0(register_5_q[0]), .S1(register_5_q[1]), .I0(and_1_out), .I1(or_1_out), .I2(fa_1_sum),
    .O(mux_3to1_1_o[0]));
  Mux_3to1 mux_3to1_2 (
    .S0(register_5_q[0]), .S1(register_5_q[1]), .I0(and_3_out), .I1(or_2_out), .I2(fa_2_sum),
    .O(mux_3to1_1_o[1]));
  Mux_3to1 mux_3to1_3 (
    .S0(register_5_q[0]), .S1(register_5_q[1]), .I0(and_4_out), .I1(or_3_out), .I2(fa_3_sum),
    .O(mux_3to1_1_o[2]));
  Mux_3to1 mux_3to1_4 (
    .S0(register_5_q[0]), .S1(register_5_q[1]), .I0(and_5_out), .I1(or_4_out), .I2(fa_4_sum),
    .O(mux_3to1_1_o[3]));
  Register #(.trigger("falling"), .width(4)) register_6 (.D(mux_3to1_1_o), .clk(Clk), .Q(Result));  // open: en, clr
  and and_6 (and_6_out, ~register_4_q, ~register_3_q, register_5_q[1], ~register_5_q[0]);  // AND_Gate
  and and_7 (and_7_out, ~register_1_q[3], ~register_2_q[3], mux_3to1_1_o[3]);  // AND_Gate
  and and_8 (and_8_out, register_1_q[3], register_2_q[3], ~mux_3to1_1_o[3]);  // AND_Gate
  and and_9 (and_9_out, ~register_4_q, register_3_q, register_5_q[1], ~register_5_q[0]);  // AND_Gate
  and and_10 (and_10_out, register_1_q[3], ~register_2_q[3], ~mux_3to1_1_o[3]);  // AND_Gate
  and and_11 (and_11_out, ~register_1_q[3], register_2_q[3], mux_3to1_1_o[3]);  // AND_Gate
  and and_12 (and_17_out[1], ~mux_3to1_1_o[0], ~mux_3to1_1_o[1], ~mux_3to1_1_o[2], ~mux_3to1_1_o[3]);  // AND_Gate
  and and_13 (and_13_out, and_6_out, and_7_out);
  and and_14 (and_14_out, and_6_out, and_8_out);
  and and_15 (and_15_out, and_9_out, and_10_out);
  and and_16 (and_16_out, and_9_out, and_11_out);
  xor xor_1 (xor_1_out, mux_3to1_1_o[3], and_17_out[2]);
  or or_5 (and_17_out[2], and_13_out, and_14_out, and_15_out, and_16_out);
  and and_17 (and_17_out[0], register_5_q[1], ~register_5_q[0], xor_1_out);  // AND_Gate
  Register #(.trigger("falling"), .width(3)) register_7 (.D(and_17_out), .clk(Clk), .Q(Status));  // open: en, clr

  // Notes on the sheet:
  //   Colette Li 261098318
endmodule

module Mux_2to1 (
  input  S,
  input  A,
  input  B,
  output O
);

  wire and_1_out, and_2_out, not_1_out;

  not not_1 (not_1_out, S);
  and and_1 (and_1_out, A, not_1_out);
  and and_2 (and_2_out, S, B);
  or or_1 (O, and_1_out, and_2_out);
endmodule

module FA (
  input  CarryIn,
  input  A,
  input  B,
  output Sum,
  output CarryOut
);

  wire ha_1_carry, ha_1_sum, ha_2_carry;

  HA ha_1 (.A(A), .B(B), .Sum(ha_1_sum), .Carry(ha_1_carry));
  HA ha_2 (.A(CarryIn), .B(ha_1_sum), .Sum(Sum), .Carry(ha_2_carry));
  or or_1 (CarryOut, ha_2_carry, ha_1_carry);
endmodule

module HA (
  input  A,
  input  B,
  output Sum,
  output Carry
);

  xor xor_1 (Sum, A, B);
  and and_1 (Carry, B, A);
endmodule

module Mux_3to1 (
  input  S0,
  input  S1,
  input  I0,
  input  I1,
  input  I2,
  output O
);

  wire mux_2to1_1_o;

  Mux_2to1 mux_2to1_1 (.S(S0), .A(I0), .B(I1), .O(mux_2to1_1_o));
  Mux_2to1 mux_2to1_2 (.S(S1), .A(mux_2to1_1_o), .B(I2), .O(O));
endmodule
